# Fritzing sketch SpeedRacer (saved by Fritzing 0.9.3b)
breadboards: 1

parts:
  Track_1 = Toggle Switch [package=THT]
  Track_2 = Toggle Switch [package=THT]
  Track_3 = Toggle Switch [package=THT]
  Start_Switch = Toggle Switch [package=THT]
  R1 = Resistor [tolerance=±5% resistance=220 package=THT]
  R2 = Resistor [tolerance=±5% resistance=220 package=THT]
  R3 = Resistor [tolerance=±5% resistance=220 package=THT]
  R4 = Resistor [tolerance=±5% resistance=220 package=THT]
  Raspberry_Pi_1 = Raspberry Pi 3 [part_number=RPI-3-V1.2]
  LED1 = smd LED [color="Red (633nm)" package="0805 [SMD]"]  # not connected

nets:
  N1: Track_1.L1, R1.Pin_1, Raspberry_Pi_1.GPIO13
  N2: Track_1.COM, Track_2.COM, Track_3.COM, Start_Switch.COM, Raspberry_Pi_1.3v3
  N3: Track_2.L1, R2.Pin_1, Raspberry_Pi_1.GPIO19
  N4: Track_3.L1, R3.Pin_1, Raspberry_Pi_1.GPIO26
  N5: Start_Switch.L1, R4.Pin_1, Raspberry_Pi_1.GPIO6
  N6: R1.Pin_0, R2.Pin_0, R3.Pin_0, R4.Pin_0, Raspberry_Pi_1.GPIO5, Raspberry_Pi_1.GND

notes:
  SpeedRacer Wiring Diagram
  -All switches shown are standard limit swtches
  -RaspberryPi V3 Model B
  Visit
  https://github.com/ctrezevant/speedRacer
  for more information.
